// Logisim project CPU.circ as structural Verilog: 5 circuits, main circuit main
module main (
);

  wire [31:0] PC_q, rom_1_data;

  Register #(.width(32)) PC (.Q(PC_q));  // open: D, en, clk, clr
  ROM #(.addrWidth(24), .dataWidth(32)) rom_1 (.addr(PC_q[23:0]), .data(rom_1_data));
  Reg32 reg32_1 ();  // open: RegWrite, WriteReg, WriteData, ReadReg1, ReadReg2, Reset, ReadData1, ReadData2
  RAM ram_1 ();  // open: addr, we, oe, clk, din, dout
  Control control_1 (.Instruction(rom_1_data[5:0]));  // open: RegDst, Jump, Branch, MemRead, MemtoReg, ALUOp, MemWrite, ALUSrc, RegWrite
  ALU alu_1 ();  // open: A, B, ALU_OP, ALU_Result
  ALU_control alu_control_1 ();  // open: ALUOp, funct, ALU_operation
  // Pins of 24 and 32 bits meet at PC_q
endmodule

module Reg32 (
  input  RegWrite,
  input  [4:0] WriteReg,
  input  [31:0] WriteData,
  input  [4:0] ReadReg1,
  input  [4:0] ReadReg2,
  input  Reset,
  output [31:0] ReadData1,
  output [31:0] ReadData2
);

  wire CLK, W0, W1, W2, W3, W4, W5, W6, W7, W8, W9, W10, W11, W12, W13, W14, W15, W16, W17, W18, W19, W20,
       W21, W22, W23, W24, W25, W26, W27, W28, W29, W30, W31;
  wire [31:0] R0, R1, R2, R3, R4, R5, R6, R7, R8, R9, R10, R11, R12, R13, R14, R15, R16, R17, R18, R19, R20,
       R21, R22, R23, R24, R25, R26, R27, R28, R29, R30, R31;

  Register #(.width(32)) register_1 (.D({32{1'b0}}), .en(W0), .clk(CLK), .Q(R0), .clr(Reset));
  Register #(.width(32)) register_2 (.D(WriteData), .en(W4), .clk(CLK), .Q(R4), .clr(Reset));
  Register #(.width(32)) register_3 (.D(WriteData), .en(W8), .clk(CLK), .Q(R8), .clr(Reset));
  Register #(.width(32)) register_4 (.D(WriteData), .en(W12), .clk(CLK), .Q(R12), .clr(Reset));
  Register #(.width(32)) register_5 (.D(WriteData), .en(W16), .clk(CLK), .Q(R16), .clr(Reset));
  Register #(.width(32)) register_6 (.D(WriteData), .en(W20), .clk(CLK), .Q(R20), .clr(Reset));
  Register #(.width(32)) register_7 (.D(WriteData), .en(W24), .clk(CLK), .Q(R24), .clr(Reset));
  Register #(.width(32)) register_8 (.D(WriteData), .en(W28), .clk(CLK), .Q(R28), .clr(Reset));
  Register #(.width(32)) register_9 (.D(WriteData), .en(W1), .clk(CLK), .Q(R1), .clr(Reset));
  Register #(.width(32)) register_10 (.D(WriteData), .en(W5), .clk(CLK), .Q(R5), .clr(Reset));
  Register #(.width(32)) register_11 (.D(WriteData), .en(W9), .clk(CLK), .Q(R9), .clr(Reset));
  Register #(.width(32)) register_12 (.D(WriteData), .en(W13), .clk(CLK), .Q(R13), .clr(Reset));
  Register #(.width(32)) register_13 (.D(WriteData), .en(W17), .clk(CLK), .Q(R17), .clr(Reset));
  Register #(.width(32)) register_14 (.D(WriteData), .en(W21), .clk(CLK), .Q(R21), .clr(Reset));
  Register #(.width(32)) register_15 (.D(WriteData), .en(W25), .clk(CLK), .Q(R25), .clr(Reset));
  Register #(.width(32)) register_16 (.D(WriteData), .en(W29), .clk(CLK), .Q(R29), .clr(Reset));
  Register #(.width(32)) register_17 (.D(WriteData), .en(W2), .clk(CLK), .Q(R2), .clr(Reset));
  Register #(.width(32)) register_18 (.D(WriteData), .en(W6), .clk(CLK), .Q(R6), .clr(Reset));
  Register #(.width(32)) register_19 (.D(WriteData), .en(W10), .clk(CLK), .Q(R10), .clr(Reset));
  Register #(.width(32)) register_20 (.D(WriteData), .en(W14), .clk(CLK), .Q(R14), .clr(Reset));
  Register #(.width(32)) register_21 (.D(WriteData), .en(W18), .clk(CLK), .Q(R18), .clr(Reset));
  Register #(.width(32)) register_22 (.D(WriteData), .en(W22), .clk(CLK), .Q(R22), .clr(Reset));
  Register #(.width(32)) register_23 (.D(WriteData), .en(W26), .clk(CLK), .Q(R26), .clr(Reset));
  Register #(.width(32)) register_24 (.D(WriteData), .en(W30), .clk(CLK), .Q(R30), .clr(Reset));
  Register #(.width(32)) register_25 (.D(WriteData), .en(W3), .clk(CLK), .Q(R3), .clr(Reset));
  Register #(.width(32)) register_26 (.D(WriteData), .en(W7), .clk(CLK), .Q(R7), .clr(Reset));
  Register #(.width(32)) register_27 (.D(WriteData), .en(W11), .clk(CLK), .Q(R11), .clr(Reset));
  Register #(.width(32)) register_28 (.D(WriteData), .en(W15), .clk(CLK), .Q(R15), .clr(Reset));
  Register #(.width(32)) register_29 (.D(WriteData), .en(W19), .clk(CLK), .Q(R19), .clr(Reset));
  Register #(.width(32)) register_30 (.D(WriteData), .en(W23), .clk(CLK), .Q(R23), .clr(Reset));
  Register #(.width(32)) register_31 (.D(WriteData), .en(W27), .clk(CLK), .Q(R27), .clr(Reset));
  Register #(.width(32)) register_32 (.D(WriteData), .en(W31), .clk(CLK), .Q(R31), .clr(Reset));
  Clock clock_1 (.out(CLK));
  Multiplexer #(.select(5), .width(32)) multiplexer_1 (
    .in0(R0), .in1(R1), .in2(R2), .in3(R3), .in4(R4), .in5(R5), .in6(R6), .in7(R7), .in8(R8), .in9(R9),
    .in10(R10), .in11(R11), .in12(R12), .in13(R13), .in14(R14), .in15(R15), .in16(R16), .in17(R17),
    .in18(R18), .in19(R19), .in20(R20), .in21(R21), .in22(R22), .in23(R23), .in24(R24), .in25(R25),
    .in26(R26), .in27(R27), .in28(R28), .in29(R29), .in30(R30), .in31(R31), .out(ReadData1), .sel(ReadReg1));
  Multiplexer #(.select(5), .width(32)) multiplexer_2 (
    .in0(R0), .in1(R1), .in2(R2), .in3(R3), .in4(R4), .in5(R5), .in6(R6), .in7(R7), .in8(R8), .in9(R9),
    .in10(R10), .in11(R11), .in12(R12), .in13(R13), .in14(R14), .in15(R15), .in16(R16), .in17(R17),
    .in18(R18), .in19(R19), .in20(R20), .in21(R21), .in22(R22), .in23(R23), .in24(R24), .in25(R25),
    .in26(R26), .in27(R27), .in28(R28), .in29(R29), .in30(R30), .in31(R31), .out(ReadData2), .sel(ReadReg2));
  Decoder #(.select(5)) decoder_1 (
    .out0(W0), .out1(W1), .out2(W2), .out3(W3), .out4(W4), .out5(W5), .out6(W6), .out7(W7), .out8(W8),
    .out9(W9), .out10(W10), .out11(W11), .out12(W12), .out13(W13), .out14(W14), .out15(W15), .out16(W16),
    .out17(W17), .out18(W18), .out19(W19), .out20(W20), .out21(W21), .out22(W22), .out23(W23), .out24(W24),
    .out25(W25), .out26(W26), .out27(W27), .out28(W28), .out29(W29), .out30(W30), .out31(W31),
    .sel(WriteReg), .en(RegWrite));

  // Other names for the same wires on the sheet: R = Reset; WD[31:0] = WriteData
endmodule

module ALU (
  input  [31:0] A,
  input  [31:0] B,
  input  [2:0] ALU_OP,
  output [31:0] ALU_Result
);

  wire [0:0] SLT;
  wire [31:0] ADD, LAND, LNOR, LOR, SUB;

  Adder #(.width(32)) adder_1 (.a(A), .b(B), .out(ADD));  // open: cin, cout
  Subtractor #(.width(32)) subtractor_1 (.a(A), .b(B), .out(SUB));  // open: bin, bout
  assign LAND = A & B;  // AND_Gate and_1, 32 bits wide
  assign LOR = A | B;  // OR_Gate or_1, 32 bits wide
  assign LNOR = ~LOR;  // NOT_Gate not_1, 32 bits wide
  Comparator #(.width(32)) comparator_1 (.a(A), .b(B), .lt(SLT[0]));  // open: gt, eq
  Multiplexer #(.select(3), .width(32)) multiplexer_1 (
    .in0(ADD), .in1(SUB), .in2(LAND), .in3(LOR), .in4(LNOR), .in5({{31{1'b0}}, SLT[0]}), .out(ALU_Result),
    .sel(ALU_OP));  // open: in6, in7
endmodule

module ALU_control (
  input  [1:0] ALUOp,
  input  [5:0] funct,
  output [3:0] ALU_operation
);

  wire and_2_out, and_3_out, and_4_out, and_5_out, and_6_out, and_7_out, and_8_out, and_9_out, and_10_out,
       and_11_out, not_1_out, not_2_out, not_3_out, not_4_out;

  not not_1 (not_1_out, ALUOp[1]);
  not not_2 (not_2_out, funct[3]);
  not not_3 (not_3_out, funct[2]);
  not not_4 (not_4_out, funct[1]);
  and and_1 (ALU_operation[3], ALUOp[1], funct[2], funct[1]);
  and and_2 (and_2_out, ALUOp[0], not_2_out);
  and and_3 (and_3_out, ALUOp[0], funct[0]);
  and and_4 (and_4_out, ALUOp[0], funct[1]);
  and and_5 (and_5_out, ALUOp[0], funct[2]);
  and and_6 (and_6_out, ALUOp[0], funct[4]);
  and and_7 (and_7_out, ALUOp[0], funct[5]);
  and and_8 (and_8_out, ALUOp[1], funct[1]);
  and and_9 (and_9_out, ALUOp[1], ALUOp[0]);
  or or_1 (ALU_operation[1], not_1_out, not_3_out);
  and and_10 (and_10_out, ALUOp[1], not_4_out, funct[0]);
  and and_11 (and_11_out, ALUOp[1], funct[3]);
  or or_2 (ALU_operation[0], and_10_out, and_11_out);
  or or_3 (ALU_operation[2], and_2_out, and_3_out, and_4_out, and_5_out, and_6_out, and_7_out, and_8_out, and_9_out);
endmodule

module Control (
  input  [5:0] Instruction,
  output RegDst,
  output Jump,
  output Branch,
  output MemRead,
  output MemtoReg,
  output [1:0] ALUOp,
  output MemWrite,
  output ALUSrc,
  output RegWrite
);

  wire and_4_out, and_5_out, not_2_out, not_3_out, not_4_out, not_5_out;

  not not_1 (RegDst, Instruction[5]);
  not not_2 (not_2_out, Instruction[3]);
  not not_3 (not_3_out, Instruction[2]);
  not not_4 (not_4_out, Instruction[1]);
  not not_5 (not_5_out, Instruction[0]);
  and and_1 (Jump, Instruction[1], not_5_out);
  and and_2 (MemRead, not_2_out, Instruction[0]);
  and and_3 (ALUOp[1], RegDst, not_3_out);
  and and_4 (and_4_out, not_3_out, not_4_out);
  or or_1 (RegWrite, and_4_out, and_5_out);
  and and_5 (and_5_out, Instruction[5], not_2_out);

  assign ALUOp[0] = Instruction[2];
  assign ALUSrc = Instruction[0];
  assign Branch = Instruction[2];
  assign MemtoReg = Instruction[0];
  assign MemWrite = Instruction[3];
endmodule
